// Logisim project IT012_Lab02_21520027.circ as structural Verilog: 9 circuits, main circuit Warmup
module Warmup (
  input  [7:0] A,
  input  [7:0] B,
  output [7:0] S
);

  Adder adder_1 (.a(A), .b(B), .out(S));  // open: cin, cout
endmodule

module FA (
  input  A,
  input  B,
  input  Cin,
  output S,
  output Cout
);

  wire and_1_out, and_2_out, xor_1_out;

  xor xor_1 (xor_1_out, A, B);
  and and_1 (and_1_out, A, B);
  xor xor_2 (S, xor_1_out, Cin);
  and and_2 (and_2_out, xor_1_out, Cin);
  or or_1 (Cout, and_1_out, and_2_out);
endmodule

module ADDSUB4 (
  input  [3:0] A,
  input  [3:0] B,
  input  SUB,
  output C1,
  output [3:0] S,
  output C2,
  output C3,
  output C
);

  wire B_prime_1_out, B_prime_2_out, B_prime_3_out, B_prime_4_out;

  xor B_prime_1 (B_prime_1_out, B[0], SUB);
  xor B_prime_2 (B_prime_2_out, B[1], SUB);
  xor B_prime_3 (B_prime_3_out, B[2], SUB);
  xor B_prime_4 (B_prime_4_out, B[3], SUB);
  FA fa_1 (.A(A[0]), .B(B_prime_1_out), .Cin(SUB), .S(S[0]), .Cout(C1));
  FA fa_2 (.A(A[1]), .B(B_prime_2_out), .Cin(C1), .S(S[1]), .Cout(C2));
  FA fa_3 (.A(A[2]), .B(B_prime_3_out), .Cin(C2), .S(S[2]), .Cout(C3));
  FA fa_4 (.A(A[3]), .B(B_prime_4_out), .Cin(C3), .S(S[3]), .Cout(C));
endmodule

module ALU8 (
  input  [7:0] A,
  input  [7:0] B,
  input  [2:0] OP,
  output Z,
  output [7:0] R,
  output LT
);

  wire [7:0] adder_1_out, adder_2_out, and_1_out, multiplexer_1_out, multiplexer_2_out, not_1_out, or_1_out,
       subtractor_1_out, subtractor_2_out, xor_1_out;

  Adder adder_1 (.a(A), .b(B), .out(adder_1_out));  // open: cin, cout
  Adder adder_2 (.a(A), .b(8'h1), .out(adder_2_out));  // open: cin, cout
  Subtractor subtractor_1 (.a(A), .b(B), .out(subtractor_1_out));  // open: bin, bout
  Subtractor subtractor_2 (.a(A), .b(8'h1), .out(subtractor_2_out));  // open: bin, bout
  assign and_1_out = A & B;  // AND_Gate and_1, 8 bits wide
  assign or_1_out = A | B;  // OR_Gate or_1, 8 bits wide
  assign not_1_out = ~A;  // NOT_Gate not_1, 8 bits wide
  assign xor_1_out = A ^ B;  // XOR_Gate xor_1, 8 bits wide
  Multiplexer #(.select(2), .width(8)) multiplexer_1 (
    .in0(adder_1_out), .in1(adder_2_out), .in2(subtractor_1_out), .in3(subtractor_2_out),
    .out(multiplexer_1_out), .sel(OP[1:0]));  // open: en
  Multiplexer #(.select(2), .width(8)) multiplexer_2 (
    .in0(and_1_out), .in1(or_1_out), .in2(not_1_out), .in3(xor_1_out), .out(multiplexer_2_out), .sel(OP[1:0]));  // open: en
  Multiplexer #(.width(8)) multiplexer_3 (
    .in0(multiplexer_1_out), .in1(multiplexer_2_out), .out(R), .sel(OP[2]));  // open: en
  LT lt_1 (.A(A), .B(B), .R(R), .LT(LT));
  nor nor_1 (Z, R[0], R[1], R[2], R[3], R[4], R[5], R[6], R[7]);
endmodule

module LT (
  input  [7:0] A,
  input  [7:0] B,
  input  [7:0] R,
  output LT
);

  wire and_1_out, and_2_out, and_3_out, not_1_out;

  not not_1 (not_1_out, B[7]);
  and and_1 (and_1_out, A[7], not_1_out);
  and and_2 (and_2_out, not_1_out, R[7]);
  and and_3 (and_3_out, A[7], R[7]);
  or or_1 (LT, and_1_out, and_2_out, and_3_out);
endmodule

module DLATCH (
  input  D,
  input  E,
  output Q
);

  Multiplexer multiplexer_1 (.in0(Q), .in1(D), .out(Q), .sel(E));  // open: en
endmodule

module TN3 (
  input  D,
  input  CLK,
  output Q1,
  output Q2,
  output QL1,
  output QL2,
  output QF2,
  output QF1
);

  DLATCH dlatch_1 (.D(D), .E(CLK), .Q(QL1));
  DLATCH dlatch_2 (.D(D), .E(CLK), .Q(Q1));
  D_Flip_Flop d_ff_1 (.clk(CLK), .D(D), .Q(Q2));  // open: Qn, preset, en, reset
  D_Flip_Flop d_ff_2 (.clk(CLK), .D(D), .Q(QF1));  // open: Qn, preset, en, reset
  DLATCH dlatch_3 (.D(QL1), .E(CLK), .Q(QL2));
  D_Flip_Flop d_ff_3 (.clk(CLK), .D(QF1), .Q(QF2));  // open: Qn, preset, en, reset
endmodule

module REGFILE (
  input  [7:0] DIN,
  input  [1:0] RA,
  input  WE,
  input  [1:0] RD,
  input  [1:0] RB,
  input  CLK,
  output [7:0] R0,
  output [7:0] QA,
  output [7:0] R1,
  output [7:0] R2,
  output [7:0] QB,
  output [7:0] R3
);

  wire decoder_1_out0, decoder_1_out1, decoder_1_out2, decoder_1_out3;

  Decoder #(.select(2), .disabled(0)) decoder_1 (
    .out0(decoder_1_out0), .out1(decoder_1_out1), .out2(decoder_1_out2), .out3(decoder_1_out3), .sel(RD),
    .en(WE));
  Register register_1 (.D(DIN), .en(decoder_1_out0), .Q(R0), .clk(CLK));  // open: clr
  Register register_2 (.D(DIN), .en(decoder_1_out1), .Q(R1), .clk(CLK));  // open: clr
  Register register_3 (.D(DIN), .en(decoder_1_out2), .Q(R2), .clk(CLK));  // open: clr
  Register register_4 (.D(DIN), .en(decoder_1_out3), .Q(R3), .clk(CLK));  // open: clr
  Multiplexer #(.select(2), .width(8)) multiplexer_1 (
    .in0(R0), .in1(R1), .in2(R2), .in3(R3), .out(QA), .sel(RA));  // open: en
  Multiplexer #(.select(2), .width(8)) multiplexer_2 (
    .in0(R0), .in1(R1), .in2(R2), .in3(R3), .out(QB), .sel(RB));  // open: en
endmodule

module DATAPATH (
  input  [7:0] IMM,
  input  [1:0] RA,
  input  WE,
  input  SRC,
  input  [1:0] RD,
  input  [1:0] RB,
  input  CLK,
  input  [2:0] OP,
  output [7:0] R0,
  output [7:0] R1,
  output [7:0] R2,
  output [7:0] R3,
  output Z,
  output [7:0] R
);

  wire [7:0] multiplexer_1_out, REGFILE_qa, REGFILE_qb;

  REGFILE REGFILE (
    .DIN(multiplexer_1_out), .RA(RA), .WE(WE), .RD(RD), .RB(RB), .CLK(CLK), .R0(R0), .QA(REGFILE_qa),
    .R1(R1), .R2(R2), .QB(REGFILE_qb), .R3(R3));
  ALU8 ALU8 (.A(REGFILE_qa), .B(REGFILE_qb), .OP(OP), .Z(Z), .R(R));  // open: LT
  Multiplexer #(.width(8)) multiplexer_1 (.in0(R), .in1(IMM), .out(multiplexer_1_out), .sel(SRC));  // open: en
endmodule
